# Fritzing sketch AmpelSchaltung (saved by Fritzing 0.9.4)
breadboards: 1

parts:
  Raspberry_Pi_1 = Raspberry Pi 3 [part_number=RPI-3-V1.2]
  LED1 = LED - 5mm [color="Red (633nm)" package="5 mm [THT]"]
  R1 = Resistor [tolerance=±5% resistance=510 package=THT]
  LED2 = LED - 5mm [color="Yellow (595nm)" package="5 mm [THT]"]
  R2 = Resistor [tolerance=±5% resistance=510 package=THT]
  LED3 = LED - 5mm [color="Green (555nm)" package="5 mm [THT]"]
  R3 = Resistor [tolerance=±5% resistance=510 package=THT]
  S1 = Pushbutton [package="[THT]"]
  R4 = Resistor [tolerance=±5% resistance=82k package=THT]

nets:
  N1: Raspberry_Pi_1.3v3, S1.Pin_1, S1.Pin_2
  N2: Raspberry_Pi_1.GND, LED1.anode, LED2.anode, LED3.anode, R4.Pin_1
  N3: Raspberry_Pi_1.GPIO17, R3.Pin_0
  N4: Raspberry_Pi_1.GPIO27, R2.Pin_0
  N5: Raspberry_Pi_1.GPIO22, R1.Pin_0
  N6: Raspberry_Pi_1.GPIO24, S1.Pin_3, S1.Pin_4, R4.Pin_0
  N7: LED1.cathode, R1.Pin_1
  N8: LED2.cathode, R2.Pin_1
  N9: LED3.cathode, R3.Pin_1
